# Fritzing sketch Untitled Sketch 3 (saved by Fritzing 0.9.3b)
breadboards: 1

parts:
  J1 = Basic Servo
  Part1 = Arduino Uno (Rev3) - ICSP
  R1 = Resistor [tolerance=±5% resistance=220 package=THT]
  R2 = Resistor [tolerance=±5% resistance=220 package=THT]
  S1 = Pushbutton [package="[THT]"]
  S2 = Pushbutton [package="[THT]"]
  R3 = Resistor [tolerance=±5% resistance=220 package="0805 [SMD]"]
  R4 = Resistor [tolerance=±5% resistance=220 package="0805 [SMD]"]

nets:
  GND: J1.gnd, Part1.GND, R1.Pin_0, R2.Pin_0, R3.Pin_0, R4.Pin_0
  VCC: J1.vcc, Part1.5V, S1.Pin_1, S1.Pin_2, S2.Pin_1, S2.Pin_2
  N1: Part1.D11_PWM/MOSI, S2.Pin_3, S2.Pin_4, R4.Pin_1
  N2: Part1.D12/MISO, S1.Pin_3, S1.Pin_4, R3.Pin_1

// code stored in the sketch: Untitled3.ino
#include <Servo.h>

Servo myservo;

int potpin = 0;
int val = 0;
const int buttonPin1 = 11;
const int buttonPin2 = 12;
int servoPin = 9;
int buttonState1 = 0;
int buttonState2 = 0;

void setup() {
  Serial.begin(9600);
  myservo.attach(servoPin);
  pinMode(buttonPin1, INPUT);
  pinMode(buttonPin2, INPUT);

}

void loop() {
  buttonState1 = digitalRead(buttonPin1);
  buttonState2 = digitalRead(buttonPin2);

  if (buttonState1 == HIGH) {
    Serial.println(val);
    myservo.write(val++);

  }
  if (buttonState2 == HIGH) {
    Serial.println("Button 2 is on");
    myservo.write(val--);
    delay(15);

  }
}
